# Fritzing sketch Conexion EMISOR (saved by Fritzing 1.0.5)
breadboards: 1

parts:
  M1 = DOIT Esp32 DevKit v1 (30 pins long, 11 pins width) [part_number=ESP32S-PIN30]
  Mod1 = RYLR896 [package=THT]
  LED1 = LED - 5mm [color="Red (633nm)" current=0.030A package="5 mm [THT]"]
  S1 = Pushbutton [package=THT]
  S2 = Pushbutton [package=THT]

nets:
  N1: M1.3V3, Mod1.pin1
  N2: M1.GND, Mod1.pin5, LED1.cathode, S1.leg1, S2.leg1
  N3: M1.RX2, Mod1.pin4
  N4: M1.TX2, Mod1.pin3#3
  N5: M1.D21, S1.leg0
  N6: M1.D22, S2.leg0
  N7: M1.D23, LED1.anode

custom parts:
  DOIT Esp32 DevKit v1 (30 pins long, 11 pins width): The DOIT Esp32 DevKit v1 is one of the development board created by DOIT to evaluate the ESP-WROOM-32 module. It is based on the ESP32 microcontroller that boasts Wifi, Bluetooth, Ethernet and Low Power support all in a single chip. (vanepp) made breadboard work, adjusted pin numbering and labels and reduced size of schematic and cleaned up pcb. This chip is 30pins long (2 x15) and 11 pins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
  RYLR896: RYLR896 UART Interface 868/915mhz LORA Transceiver Module
